// Logisim project Mealy1101out10_1011out01_otherwise11.circ as structural Verilog: 1 circuit, main circuit main
module main (
  input  in_1,
  output out_2,
  output out_3
);

  wire and_1_out, and_2_out, and_3_out, and_4_out, and_5_out, and_6_out, and_7_out, and_8_out, and_9_out,
       and_10_out, and_11_out, and_12_out, clock_1_out, d_ff_1_q, d_ff_1_qn, d_ff_2_q, d_ff_2_qn, d_ff_3_q,
       d_ff_3_qn, not_1_out, or_1_out, or_2_out, or_3_out;

  Clock clock_1 (.out(clock_1_out));
  not not_1 (not_1_out, in_1);
  D_Flip_Flop d_ff_1 (.D(or_1_out), .clk(clock_1_out), .Q(d_ff_1_q), .Qn(d_ff_1_qn));  // open: preset, reset
  D_Flip_Flop d_ff_2 (.D(or_2_out), .clk(clock_1_out), .Q(d_ff_2_q), .Qn(d_ff_2_qn));  // open: preset, reset
  D_Flip_Flop d_ff_3 (.D(or_3_out), .clk(clock_1_out), .Q(d_ff_3_q), .Qn(d_ff_3_qn));  // open: preset, reset
  and and_1 (and_1_out, not_1_out, d_ff_3_q, d_ff_2_qn);
  and and_2 (and_2_out, d_ff_1_qn, in_1, d_ff_3_q, d_ff_2_q);
  and and_3 (and_3_out, d_ff_1_q, d_ff_2_qn, d_ff_3_qn, in_1);
  and and_4 (and_4_out, d_ff_2_qn, d_ff_3_qn, in_1);
  and and_5 (and_5_out, d_ff_1_qn, d_ff_2_q, d_ff_3_qn, not_1_out);
  and and_6 (and_6_out, d_ff_1_qn, d_ff_2_q, d_ff_3_q, in_1);
  and and_7 (and_7_out, d_ff_2_qn, not_1_out, d_ff_3_q, d_ff_1_q);
  or or_1 (or_1_out, and_1_out, and_2_out, and_3_out);
  and and_8 (and_8_out, d_ff_2_qn, d_ff_3_q, in_1);
  and and_9 (and_9_out, d_ff_1_qn, d_ff_2_q, d_ff_3_qn);
  or or_2 (or_2_out, and_8_out, and_9_out);
  or or_3 (or_3_out, and_4_out, and_5_out, and_6_out, and_7_out);
  and and_10 (and_10_out, d_ff_1_qn, d_ff_2_qn);
  and and_11 (and_11_out, d_ff_3_q, not_1_out);
  and and_12 (and_12_out, d_ff_1_q, d_ff_2_q);
  or or_4 (out_2, d_ff_1_qn, and_12_out, d_ff_3_qn);
  or or_5 (out_3, d_ff_1_q, and_10_out, and_11_out, d_ff_3_qn);
  // PlaRom #(.Contents("0 1 2 1 1 2*3 0*8 1*3 0"), .outputs(1)) plarom_1: pin names not known; wires that end beside it: not_1_out
endmodule
