// Logisim project Ex4.circ as structural Verilog: 1 circuit, main circuit main
module main (
  output [2:0] out_1
);

  wire and_1_out, and_2_out, and_3_out, and_4_out, clock_1_out, d_ff_1_qn, d_ff_2_qn, d_ff_3_qn, or_1_out,
       xor_1_out;

  Clock clock_1 (.out(clock_1_out));
  D_Flip_Flop d_ff_1 (.D(d_ff_1_qn), .clk(clock_1_out), .Q(out_1[0]), .Qn(d_ff_1_qn));  // open: preset, reset
  xor xor_1 (xor_1_out, out_1[1], out_1[0]);
  and and_1 (and_1_out, out_1[0], out_1[1]);
  D_Flip_Flop d_ff_2 (.D(xor_1_out), .clk(clock_1_out), .Q(out_1[1]), .Qn(d_ff_2_qn));  // open: preset, reset
  and and_2 (and_2_out, and_1_out, d_ff_3_qn);
  and and_3 (and_3_out, d_ff_1_qn, out_1[2]);
  and and_4 (and_4_out, out_1[2], d_ff_2_qn);
  D_Flip_Flop d_ff_3 (.D(or_1_out), .clk(clock_1_out), .Q(out_1[2]), .Qn(d_ff_3_qn));  // open: preset, reset
  or or_1 (or_1_out, and_2_out, and_3_out, and_4_out);

  // Notes on the sheet:
  //   Dc = NOT Qc
  //   LSB
  //   Db = Qb XOR Qc
  //   (NOT A) & B & C
  //   A & (NOT C)
  //   A & (NOT B)
  //   MSB
endmodule
