// Logisim project Ex5.circ as structural Verilog: 1 circuit, main circuit main
module main (
  input  in_1,
  input  in_2,
  input  in_3
);

  wire and_1_out, and_2_out, and_3_out, and_4_out, clock_1_out, j_k_ff_1_q, j_k_ff_2_q, j_k_ff_2_qn,
       j_k_ff_3_q, j_k_ff_3_qn, not_1_out, or_1_out, or_2_out, xnor_1_out, xnor_2_out;

  not not_1 (not_1_out, in_1);
  and and_1 (and_1_out, in_1, j_k_ff_3_q);
  and and_2 (and_2_out, j_k_ff_2_qn, not_1_out);
  or or_1 (or_1_out, and_1_out, and_2_out);
  Clock clock_1 (.out(clock_1_out));
  J_K_Flip_Flop j_k_ff_1 (.J(or_1_out), .K(1'b1), .clk(clock_1_out), .Q(j_k_ff_1_q));  // open: Qn, preset, reset
  and and_3 (and_3_out, in_1, j_k_ff_1_q);
  and and_4 (and_4_out, not_1_out, j_k_ff_3_qn);
  J_K_Flip_Flop j_k_ff_2 (
    .J(1'b1), .K(or_2_out), .clk(clock_1_out), .Q(j_k_ff_2_q), .Qn(j_k_ff_2_qn), .reset(in_2));  // open: preset
  or or_2 (or_2_out, and_3_out, and_4_out);
  xnor xnor_1 (xnor_1_out, in_1, j_k_ff_1_q);
  xnor xnor_2 (xnor_2_out, in_1, j_k_ff_2_q);
  J_K_Flip_Flop j_k_ff_3 (
    .J(xnor_2_out), .K(xnor_1_out), .clk(clock_1_out), .Q(j_k_ff_3_q), .Qn(j_k_ff_3_qn), .reset(in_3));  // open: preset
endmodule
