// Logisim project Ex6.circ as structural Verilog: 1 circuit, main circuit main
module main (
);

  wire bcd_to_7_segment_decoder_1_p1, clock_1_out, counter_2_carry, counter_4_carry;
  wire [3:0] counter_1_q, counter_2_q, counter_3_q, counter_4_q;

  Clock clock_1 (.out(clock_1_out));
  Counter #(.max('h5), .trigger("falling"), .width(4)) counter_1 (
    .clk(counter_2_carry), .Q(counter_1_q));  // open: clr, load, up, count, D, carry
  Counter #(.max('h9), .trigger("falling"), .width(4)) counter_2 (
    .clk(bcd_to_7_segment_decoder_1_p1), .carry(counter_2_carry), .Q(counter_2_q));  // open: clr, load, up, count, D
  _7_Segment_Display u_7_segment_display_1 ();  // open: g, f, a, b, e, d, c, dp
  // BCD_to_7_Segment_decoder bcd_to_7_segment_decoder_1: pin names not known; wires that end beside it: bcd_to_7_segment_decoder_1_p1, counter_1_q
  _7_Segment_Display u_7_segment_display_2 ();  // open: g, f, a, b, e, d, c, dp
  // BCD_to_7_Segment_decoder bcd_to_7_segment_decoder_2: pin names not known; wires that end beside it: counter_2_q
  Counter #(.max('h5), .trigger("falling"), .width(4)) counter_3 (
    .clk(counter_4_carry), .carry(bcd_to_7_segment_decoder_1_p1), .Q(counter_3_q));  // open: clr, load, up, count, D
  _7_Segment_Display u_7_segment_display_3 ();  // open: g, f, a, b, e, d, c, dp
  // BCD_to_7_Segment_decoder bcd_to_7_segment_decoder_3: pin names not known; wires that end beside it: counter_3_q
  Counter #(.max('h9), .trigger("falling"), .width(4)) counter_4 (
    .clk(clock_1_out), .carry(counter_4_carry), .Q(counter_4_q));  // open: clr, load, up, count, D
  _7_Segment_Display u_7_segment_display_4 ();  // open: g, f, a, b, e, d, c, dp
  // BCD_to_7_Segment_decoder bcd_to_7_segment_decoder_4: pin names not known; wires that end beside it: counter_4_q
endmodule
