// Logisim project 24125093_HW3_Ex01-06.circ as structural Verilog: 1 circuit, main circuit main
module main (
  input  MSB,
  input  in_2,
  input  in_3,
  input  LSB,
  input  MSB_2,
  input  in_6,
  input  in_7,
  input  LSB_2,
  input  in_9,
  input  in_10,
  input  in_11,
  input  in_12,
  input  Enable,
  input  A0,
  input  A1,
  input  A2,
  input  A3,
  input  I0,
  input  in_19,
  input  I1,
  input  I2,
  input  in_22,
  input  I3,
  input  I0_2,
  input  in_25,
  input  I1_2,
  input  I2_2,
  input  in_28,
  input  I3_2,
  input  in_30,
  input  S0,
  input  D,
  input  I0_3,
  input  I1_3,
  input  I2_3,
  input  I3_3,
  input  I4,
  input  I5,
  input  I6,
  input  I7,
  input  S0_2,
  input  S1,
  input  S2,
  input  in_44,
  input  in_45,
  input  in_46,
  input  in_47,
  output Y0,
  output Y1,
  output V,
  output _0_3,
  output _4_7,
  output out_53,
  output _8_11,
  output out_55,
  output _12_15,
  output out_57,
  output out_58,
  output out_59,
  output out_60,
  output out_61,
  output out_62,
  output out_63,
  output out_64,
  output out_65,
  output out_66,
  output out_67,
  output out_68,
  output out_69,
  output out_70,
  output _0,
  output _1,
  output _2,
  output _3,
  output _4,
  output _5,
  output _6,
  output _7
);

  wire and_1_out, and_2_out, and_3_out, and_4_out, and_5_out, and_6_out, and_7_out, and_8_out, and_9_out,
       decoder_1_out0, decoder_1_out1, decoder_1_out2, decoder_1_out3, multiplexer_1_out, multiplexer_2_out,
       nand_3_out, nand_4_out, nand_5_out, nand_6_out, nand_7_out, nand_8_out, nand_10_out, nand_11_out,
       not_1_out, not_2_out, not_3_out, not_4_out, not_5_out, not_6_out, not_7_out, not_8_out, not_9_out,
       not_10_out, not_11_out, not_12_out, not_13_out, not_14_out;
  wire [6:0] plarom_1_p2, plarom_2_p2;

  Decoder #(.select(2)) decoder_1 (
    .out0(decoder_1_out0), .out1(decoder_1_out1), .out2(decoder_1_out2), .out3(decoder_1_out3),
    .sel({A3, A2}), .en(Enable));
  Demultiplexer #(.enable("true"), .select(2)) demultiplexer_1 (
    .out0(_0), .out1(_1), .out2(_2), .out3(_3), .in(in_44), .sel({in_46, in_47}), .en(not_1_out));
  not not_1 (not_1_out, in_45);
  Demultiplexer #(.enable("true"), .select(2)) demultiplexer_2 (
    .out0(_4), .out1(_5), .out2(_6), .out3(_7), .in(in_44), .sel({in_46, in_47}), .en(in_45));
  // PlaRom #(.Contents("1*7 2 1 1 2 1*3 2 2 1 2 1*3 2 1 2 1 2 2 1 1 2*4 1*3 2 1 1 2 2 1 2 1 2 1 2*4 1 1 2 2 1 2*4 1 2*4 0 1*6 0*4 1 1 0 1 0 1 1 0 1*3 0 0 1*6 0 0 1 1 0 1 1 0 1 1 0 1*6 0 1 0*4 1*12 0 1*7 0 1*8 0*3 1*3 0 0 1 1 0 1*4 0 1*4 0 0 1*4 0*3 1"), .\and (16), .outputs(7)) plarom_1: pin names not known; wires that end beside it: {MSB, in_2, in_3, LSB}, plarom_1_p2
  // PlaRom #(.Contents("1*7 2 1 1 2 1*3 2 2 1 2 1*3 2 1 2 1 2 2 1 1 2*4 1*3 2 1 1 2 2 1 2 1 2 1 2*4 1 1 2 2 1 2*4 1 2*4 1 0*6 1*4 0 0 1 0 1 0 0 1 0*3 1 1 0*6 1 1 0 0 1 0 0 1 0 0 1 0*6 1 0 1*4 0*12 1 0*7 1 0*8 1*3 0*3 1 1 0 0 1 0*4 1 0*4 1 1 0*4 1*3 0"), .\and (16), .outputs(7)) plarom_2: pin names not known; wires that end beside it: {MSB_2, in_6, in_7, LSB_2}, plarom_2_p2
  not not_2 (not_2_out, in_11);
  // NAND_Gate nand_1 has open pins: in0=in_19, in1=in_19, out=open
  // NAND_Gate nand_2 has open pins: in0=in_22, in1=in_22, out=open
  not not_3 (not_3_out, in_30);
  not not_4 (not_4_out, S0);
  and and_1 (and_1_out, in_10, not_2_out);
  or or_1 (V, in_12, in_11, in_10, in_9);
  Decoder #(.select(2)) decoder_2 (
    .out0(_0_3), .out1(out_53), .out2(out_57), .out3(out_61), .sel({A1, A0}), .en(decoder_1_out0));
  nand nand_3 (nand_3_out, I0, in_19);
  nand nand_4 (nand_4_out, in_19, I1);
  nand nand_5 (nand_5_out, I2, in_22);
  nand nand_6 (nand_6_out, in_22, I3);
  not not_5 (not_5_out, in_25);
  not not_6 (not_6_out, in_28);
  Multiplexer #(.enable("true"), .select(2)) multiplexer_1 (
    .in0(I0_3), .in1(I1_3), .in2(I2_3), .in3(I3_3), .out(multiplexer_1_out), .sel({S1, S0_2}), .en(not_7_out));
  not not_7 (not_7_out, S2);
  Multiplexer #(.enable("true"), .select(2)) multiplexer_2 (
    .in0(I4), .in1(I5), .in2(I6), .in3(I7), .out(multiplexer_2_out), .sel({S1, S0_2}), .en(S2));
  Decoder #(.select(2)) decoder_3 (
    .out0(_4_7), .out1(out_55), .out2(out_59), .out3(out_63), .sel({A1, A0}), .en(decoder_1_out1));
  not not_8 (not_8_out, plarom_2_p2[0]);
  not not_9 (not_9_out, plarom_2_p2[1]);
  not not_10 (not_10_out, plarom_2_p2[2]);
  not not_11 (not_11_out, plarom_2_p2[3]);
  not not_12 (not_12_out, plarom_2_p2[4]);
  not not_13 (not_13_out, plarom_2_p2[5]);
  not not_14 (not_14_out, plarom_2_p2[6]);
  or or_2 (Y0, and_1_out, in_12);
  or or_3 (Y1, in_11, in_12);
  nand nand_7 (nand_7_out, nand_3_out, nand_4_out);
  nand nand_8 (nand_8_out, nand_5_out, nand_6_out);
  and and_2 (and_2_out, not_3_out, not_4_out, D);
  and and_3 (and_3_out, D, not_4_out, in_30);
  and and_4 (and_4_out, D, S0, not_3_out);
  and and_5 (and_5_out, in_30, S0, D);
  _7_Segment_Display #(.decimalPoint("false")) u_7_segment_display_1 (
    .g(plarom_1_p2[6]), .f(plarom_1_p2[5]), .a(plarom_1_p2[0]), .b(plarom_1_p2[1]), .e(plarom_1_p2[4]),
    .d(plarom_1_p2[3]), .c(plarom_1_p2[2]));
  _7_Segment_Display #(.decimalPoint("false")) u_7_segment_display_2 (
    .g(not_14_out), .f(not_13_out), .a(not_8_out), .b(not_9_out), .e(not_12_out), .d(not_11_out),
    .c(not_10_out));
  Decoder #(.select(2)) decoder_4 (
    .out0(_8_11), .out1(out_58), .out2(out_62), .out3(out_65), .sel({A1, A0}), .en(decoder_1_out2));
  and and_6 (and_6_out, I0_2, not_5_out, not_6_out);
  and and_7 (and_7_out, I1_2, in_25, not_6_out);
  and and_8 (and_8_out, not_5_out, I2_2, in_28);
  and and_9 (and_9_out, in_28, I3_2, in_25);
  or or_4 (out_70, multiplexer_1_out, multiplexer_2_out);
  Decoder #(.select(2)) decoder_5 (
    .out0(_12_15), .out1(out_60), .out2(out_64), .out3(out_66), .sel({A1, A0}), .en(decoder_1_out3));
  // NAND_Gate nand_9 has open pins: in0=1'b1, in1=1'b1, out=open
  or or_5 (out_68, and_6_out, and_7_out, and_8_out, and_9_out);
  or or_6 (out_69, and_2_out, and_3_out, and_4_out, and_5_out);
  nand nand_10 (nand_10_out, nand_7_out, 1'b1);
  nand nand_11 (nand_11_out, 1'b1, nand_8_out);
  nand nand_12 (out_67, nand_10_out, nand_11_out);

  // Notes on the sheet:
  //   S1
  //   8:1 MUX using 4:1 MUX
  //   1:8 DEMUX FROM 1:4 DEMUXes
  //   4:1 MUX using basic logic gates
  //   1:4 DEMUX using basic logic gates
  //   S2
  //   S1
  //   S0
endmodule
