// Logisim project 24125093_HW3_Ex7.circ as structural Verilog: 1 circuit, main circuit main
module main (
  input  A,
  input  B,
  input  C,
  output out_4,
  output out_5
);

  wire n74153_1_pin3, n74153_1_pin4, not_1_out;

  not not_1 (not_1_out, A);
  _74153 #(.ShowInternalStructure("true")) u_74153_1 (
    .pin2(C), .pin3(n74153_1_pin3), .pin4(n74153_1_pin4), .pin5(n74153_1_pin4), .pin6(n74153_1_pin3),
    .pin7(out_5), .pin14(B), .pin13(n74153_1_pin3), .pin12(n74153_1_pin3), .pin11(n74153_1_pin4),
    .pin10(not_1_out), .pin9(out_4));  // open: pin1, pin15
  // also tied to GND on the sheet: n74153_1_pin4
  // also tied to VCC on the sheet: n74153_1_pin3
endmodule
