// Logisim project 24125093_W05_02.circ as structural Verilog: 1 circuit, main circuit main
module main (
  input  in_1,
  input  in_2,
  input  in_3,
  input  in_4,
  input  in_5,
  input  in_6,
  output out_7,
  output out_8,
  output out_9
);

  wire and_1_out, and_2_out, and_3_out, and_4_out, and_5_out, clock_1_out, clock_2_out, clock_3_out,
       d_ff_1_q, d_ff_2_q, d_ff_3_q, d_ff_4_q, d_ff_5_q, d_ff_6_q, not_1_out, not_2_out, not_3_out,
       not_4_out, or_1_out, or_2_out;

  Clock clock_1 (.out(clock_1_out));
  Clock clock_2 (.out(clock_2_out));
  Clock clock_3 (.out(clock_3_out));
  D_Flip_Flop d_ff_1 (.D(in_1), .clk(clock_1_out), .Q(d_ff_1_q), .reset(in_2));  // open: Qn, preset
  D_Flip_Flop d_ff_2 (.D(in_3), .clk(clock_2_out), .Q(d_ff_2_q), .reset(in_4));  // open: Qn, preset
  D_Flip_Flop d_ff_3 (.D(in_5), .clk(clock_3_out), .Q(d_ff_3_q), .reset(in_6));  // open: Qn, preset
  not not_1 (not_1_out, in_1);
  not not_2 (not_2_out, in_3);
  not not_3 (not_3_out, in_5);
  and and_1 (and_1_out, d_ff_1_q, not_1_out);
  and and_2 (and_2_out, d_ff_2_q, not_2_out);
  and and_3 (and_3_out, d_ff_3_q, not_3_out);
  D_Flip_Flop d_ff_4 (.D(or_1_out), .clk(clock_1_out), .Q(d_ff_4_q), .reset(in_2));  // open: Qn, preset
  D_Flip_Flop d_ff_5 (.D(and_2_out), .clk(clock_2_out), .Q(d_ff_5_q), .reset(in_4));  // open: Qn, preset
  not not_4 (not_4_out, d_ff_3_q);
  D_Flip_Flop d_ff_6 (.D(or_2_out), .clk(clock_3_out), .Q(d_ff_6_q), .reset(in_6));  // open: Qn, preset
  and and_4 (and_4_out, d_ff_4_q, in_1);
  and and_5 (and_5_out, not_4_out, in_5, d_ff_6_q);
  or or_1 (or_1_out, and_4_out, and_1_out);
  or or_2 (or_2_out, and_5_out, and_3_out);
  and and_6 (out_8, d_ff_5_q, in_3);
  and and_7 (out_9, d_ff_6_q, d_ff_3_q, in_5);
  and and_8 (out_7, d_ff_4_q, d_ff_1_q);
endmodule
