// Logisim project lab4.circ as structural Verilog: 9 circuits, main circuit main
module main (
  input  Ex01,
  input  in_2,
  input  in_3,
  input  in_4,
  input  in_5,
  input  [3:0] in_6,
  input  [3:0] in_7,
  input  [3:0] in_8,
  input  [3:0] in_9,
  input  [3:0] in_10,
  input  [3:0] in_11,
  input  in_12,
  input  [3:0] in_13,
  input  [3:0] in_14,
  input  in_15,
  input  [3:0] in_16,
  input  [3:0] in_17,
  output out_18,
  output out_19,
  output out_20,
  output out_21,
  output out_22,
  output [3:0] out_23,
  output out_24,
  output [3:0] out_25,
  output out_26,
  output [3:0] out_27,
  output overflow,
  output [3:0] out_29,
  output out_30,
  output [3:0] out_31
);

  wire b_cell_1_g, b_cell_1_p, b_cell_2_g, b_cell_2_p, b_cell_3_g, b_cell_3_p, b_cell_4_g, b_cell_4_p,
       cla_logic_1_c1, cla_logic_1_c2, cla_logic_1_c3;

  Half_Adder_1_bit half_adder_1_bit_1 (.a(Ex01), .b(in_2), .Q(out_18), .cout(out_19));
  Full_Adder_1_bit full_adder_1_bit_1 (.cin(in_3), .a(in_4), .b(in_5), .Q(out_20), .cout(out_21));
  RCA_Adder_4_bit rca_adder_4_bit_1 (.A4(in_6), .B4(in_7), .cin(1'b0), .cout(out_22), .Q(out_23));
  RCA_Subtractor_4_bit rca_subtractor_4_bit_1 (.A4(in_8), .B4(in_9), .negative_sign(out_24), .Q(out_25));
  Add_Sub_4_bit add_sub_4_bit_1 (.A4(in_10), .B4(in_11), .C(in_12), .overflow(out_26), .Q(out_27));
  B_cell b_cell_1 (.c(cla_logic_1_c3), .x(in_13[3]), .y(in_14[3]), .G(b_cell_1_g), .s(out_29[3]), .P(b_cell_1_p));
  BCD_Adder_4_bit bcd_adder_4_bit_1 (.A(in_16), .B(in_17), .BCD_Cout(out_30), .BCD_Sum(out_31));
  B_cell b_cell_2 (.c(cla_logic_1_c2), .x(in_13[2]), .y(in_14[2]), .G(b_cell_2_g), .s(out_29[2]), .P(b_cell_2_p));
  CLA_Logic cla_logic_1 (
    .c0(in_15), .G0(b_cell_4_g), .P0(b_cell_4_p), .G1(b_cell_3_g), .P1(b_cell_3_p), .G2(b_cell_2_g),
    .P2(b_cell_2_p), .G3(b_cell_1_g), .P3(b_cell_1_p), .c1(cla_logic_1_c1), .c2(cla_logic_1_c2),
    .c3(cla_logic_1_c3), .c4(overflow));
  B_cell b_cell_3 (.c(cla_logic_1_c1), .x(in_13[1]), .y(in_14[1]), .G(b_cell_3_g), .s(out_29[1]), .P(b_cell_3_p));
  B_cell b_cell_4 (.c(in_15), .x(in_13[0]), .y(in_14[0]), .G(b_cell_4_g), .s(out_29[0]), .P(b_cell_4_p));

  // Notes on the sheet:
  //   Ex02
  //   Ex03
  //   Ex04
  //   Ex05
endmodule

module Half_Adder_1_bit (
  input  a,
  input  b,
  output Q,
  output cout
);

  xor xor_1 (Q, a, b);
  and and_1 (cout, a, b);
endmodule

module Full_Adder_1_bit (
  input  cin,
  input  a,
  input  b,
  output Q,
  output cout
);

  wire and_1_out, and_2_out, and_3_out, and_4_out, and_5_out, and_6_out, and_7_out, not_1_out, not_2_out,
       not_3_out;

  not not_1 (not_1_out, cin);
  not not_2 (not_2_out, a);
  not not_3 (not_3_out, b);
  and and_1 (and_1_out, not_1_out, not_2_out, b);
  and and_2 (and_2_out, not_1_out, a, not_3_out);
  and and_3 (and_3_out, cin, not_2_out, not_3_out);
  and and_4 (and_4_out, cin, a, b);
  and and_5 (and_5_out, a, b);
  and and_6 (and_6_out, cin, b);
  and and_7 (and_7_out, cin, a);
  or or_1 (Q, and_1_out, and_2_out, and_3_out, and_4_out);
  or or_2 (cout, and_5_out, and_6_out, and_7_out);
endmodule

module RCA_Adder_4_bit (
  input  [3:0] A4,
  input  [3:0] B4,
  input  cin,
  output cout,
  output [3:0] Q
);

  wire full_adder_1_bit_1_cout, full_adder_1_bit_2_cout, full_adder_1_bit_3_cout;

  Full_Adder_1_bit full_adder_1_bit_1 (.cin(cin), .a(A4[0]), .b(B4[0]), .Q(Q[0]), .cout(full_adder_1_bit_1_cout));
  Full_Adder_1_bit full_adder_1_bit_2 (
    .cin(full_adder_1_bit_1_cout), .a(A4[1]), .b(B4[1]), .Q(Q[1]), .cout(full_adder_1_bit_2_cout));
  Full_Adder_1_bit full_adder_1_bit_3 (
    .cin(full_adder_1_bit_2_cout), .a(A4[2]), .b(B4[2]), .Q(Q[2]), .cout(full_adder_1_bit_3_cout));
  Full_Adder_1_bit full_adder_1_bit_4 (.cin(full_adder_1_bit_3_cout), .a(A4[3]), .b(B4[3]), .Q(Q[3]), .cout(cout));
endmodule

module RCA_Subtractor_4_bit (
  input  [3:0] A4,
  input  [3:0] B4,
  output negative_sign,
  output [3:0] Q
);

  wire full_adder_1_bit_1_cout, full_adder_1_bit_2_cout, full_adder_1_bit_3_cout, full_adder_1_bit_4_cout,
       not_1_out, not_2_out, not_3_out, not_4_out;

  not not_1 (not_1_out, B4[0]);
  not not_2 (not_2_out, B4[1]);
  Full_Adder_1_bit full_adder_1_bit_1 (.cin(1'b1), .a(A4[0]), .b(not_1_out), .Q(Q[0]), .cout(full_adder_1_bit_1_cout));
  Full_Adder_1_bit full_adder_1_bit_2 (
    .cin(full_adder_1_bit_1_cout), .a(A4[1]), .b(not_2_out), .Q(Q[1]), .cout(full_adder_1_bit_2_cout));
  not not_3 (not_3_out, B4[2]);
  Full_Adder_1_bit full_adder_1_bit_3 (
    .cin(full_adder_1_bit_2_cout), .a(A4[2]), .b(not_3_out), .Q(Q[2]), .cout(full_adder_1_bit_3_cout));
  not not_4 (not_4_out, B4[3]);
  Full_Adder_1_bit full_adder_1_bit_4 (
    .cin(full_adder_1_bit_3_cout), .a(A4[3]), .b(not_4_out), .Q(Q[3]), .cout(full_adder_1_bit_4_cout));
  not not_5 (negative_sign, full_adder_1_bit_4_cout);
endmodule

module Add_Sub_4_bit (
  input  [3:0] A4,
  input  [3:0] B4,
  input  C,
  output overflow,
  output [3:0] Q
);

  wire full_adder_1_bit_1_cout, full_adder_1_bit_2_cout, full_adder_1_bit_3_cout, full_adder_1_bit_4_cout,
       xor_1_out, xor_2_out, xor_3_out, xor_4_out;

  xor xor_1 (xor_1_out, C, B4[0]);
  xor xor_2 (xor_2_out, C, B4[1]);
  Full_Adder_1_bit full_adder_1_bit_1 (.cin(C), .a(A4[0]), .b(xor_1_out), .Q(Q[0]), .cout(full_adder_1_bit_1_cout));
  xor xor_3 (xor_3_out, C, B4[2]);
  Full_Adder_1_bit full_adder_1_bit_2 (
    .cin(full_adder_1_bit_1_cout), .a(A4[1]), .b(xor_2_out), .Q(Q[1]), .cout(full_adder_1_bit_2_cout));
  Full_Adder_1_bit full_adder_1_bit_3 (
    .cin(full_adder_1_bit_2_cout), .a(A4[2]), .b(xor_3_out), .Q(Q[2]), .cout(full_adder_1_bit_3_cout));
  xor xor_4 (xor_4_out, C, B4[3]);
  Full_Adder_1_bit full_adder_1_bit_4 (
    .cin(full_adder_1_bit_3_cout), .a(A4[3]), .b(xor_4_out), .Q(Q[3]), .cout(full_adder_1_bit_4_cout));
  xor xor_5 (overflow, full_adder_1_bit_4_cout, full_adder_1_bit_3_cout);
endmodule

module B_cell (
  input  c,
  input  x,
  input  y,
  output G,
  output s,
  output P
);

  and and_1 (G, x, y);
  xor xor_1 (P, x, y);
  xor xor_2 (s, P, c);
endmodule

module CLA_Logic (
  input  c0,
  input  G0,
  input  P0,
  input  G1,
  input  P1,
  input  G2,
  input  P2,
  input  G3,
  input  P3,
  output c1,
  output c2,
  output c3,
  output c4
);

  wire and_1_out, and_2_out, and_3_out, and_4_out;

  and and_1 (and_1_out, P0, c0);
  or or_1 (c1, G0, and_1_out);
  and and_2 (and_2_out, c1, P1);
  or or_2 (c2, G1, and_2_out);
  and and_3 (and_3_out, c2, P2);
  or or_3 (c3, G2, and_3_out);
  and and_4 (and_4_out, c3, P3);
  or or_4 (c4, G3, and_4_out);
endmodule

module BCD_Adder_4_bit (
  input  [3:0] A,
  input  [3:0] B,
  output BCD_Cout,
  output [3:0] BCD_Sum
);

  wire and_1_out, and_2_out, b_cell_1_g, b_cell_1_p, b_cell_2_g, b_cell_2_p, b_cell_3_g, b_cell_3_p,
       b_cell_4_g, b_cell_4_p, b_cell_5_g, b_cell_5_p, b_cell_6_g, b_cell_6_p, b_cell_7_g, b_cell_7_p,
       b_cell_8_g, b_cell_8_p, cla_logic_1_c1, cla_logic_1_c2, cla_logic_1_c3, cla_logic_1_c4,
       cla_logic_2_c1, cla_logic_2_c2, cla_logic_2_c3;
  wire [3:0] b_cell_7_s;

  B_cell b_cell_1 (.c(cla_logic_1_c3), .x(A[3]), .y(B[3]), .G(b_cell_1_g), .s(b_cell_7_s[3]), .P(b_cell_1_p));
  B_cell b_cell_2 (.c(cla_logic_2_c3), .x(b_cell_7_s[3]), .y(1'b0), .G(b_cell_2_g), .s(BCD_Sum[3]), .P(b_cell_2_p));
  B_cell b_cell_3 (.c(cla_logic_1_c2), .x(A[2]), .y(B[2]), .G(b_cell_3_g), .s(b_cell_7_s[2]), .P(b_cell_3_p));
  CLA_Logic cla_logic_1 (
    .c0(1'b0), .G0(b_cell_7_g), .P0(b_cell_7_p), .G1(b_cell_5_g), .P1(b_cell_5_p), .G2(b_cell_3_g),
    .P2(b_cell_3_p), .G3(b_cell_1_g), .P3(b_cell_1_p), .c1(cla_logic_1_c1), .c2(cla_logic_1_c2),
    .c3(cla_logic_1_c3), .c4(cla_logic_1_c4));
  B_cell b_cell_4 (.c(cla_logic_2_c2), .x(b_cell_7_s[2]), .y(BCD_Cout), .G(b_cell_4_g), .s(BCD_Sum[2]), .P(b_cell_4_p));
  CLA_Logic cla_logic_2 (
    .c0(1'b0), .G0(b_cell_8_g), .P0(b_cell_8_p), .G1(b_cell_6_g), .P1(b_cell_6_p), .G2(b_cell_4_g),
    .P2(b_cell_4_p), .G3(b_cell_2_g), .P3(b_cell_2_p), .c1(cla_logic_2_c1), .c2(cla_logic_2_c2),
    .c3(cla_logic_2_c3));  // open: c4
  B_cell b_cell_5 (.c(cla_logic_1_c1), .x(A[1]), .y(B[1]), .G(b_cell_5_g), .s(b_cell_7_s[1]), .P(b_cell_5_p));
  and and_1 (and_1_out, b_cell_7_s[3], b_cell_7_s[2]);
  B_cell b_cell_6 (.c(cla_logic_2_c1), .x(b_cell_7_s[1]), .y(BCD_Cout), .G(b_cell_6_g), .s(BCD_Sum[1]), .P(b_cell_6_p));
  and and_2 (and_2_out, b_cell_7_s[1], b_cell_7_s[3]);
  B_cell b_cell_7 (.c(1'b0), .x(A[0]), .y(B[0]), .G(b_cell_7_g), .s(b_cell_7_s[0]), .P(b_cell_7_p));
  or or_1 (BCD_Cout, cla_logic_1_c4, and_1_out, and_2_out);
  B_cell b_cell_8 (.c(1'b0), .x(b_cell_7_s[0]), .y(1'b0), .G(b_cell_8_g), .s(BCD_Sum[0]), .P(b_cell_8_p));
endmodule
