// Logisim project lab5.circ as structural Verilog: 6 circuits, main circuit main
module main (
  input  Ex01,
  input  Ex02,
  input  [3:0] Ex03
);

  wire button_1_out, button_2_out, button_3_out, button_4_out, button_5_out, button_6_out, ex01_1_z,
       ex02_1_z, ex03_1_z;

  Button button_1 (.out(button_1_out));
  Button button_2 (.out(button_2_out));
  Button button_3 (.out(button_3_out));
  Button button_4 (.out(button_4_out));
  Button button_5 (.out(button_5_out));
  Hex_Digit_Display #(.decimalPoint("false")) hex_digit_display_1 (.value(Ex03));
  Button button_6 (.out(button_6_out));
  LED led_1 (.in(ex01_1_z));
  Ex01 ex01_1 (.Sb(Ex01), .Clock(button_1_out), .Reset(button_3_out), .Z(ex01_1_z));
  LED led_2 (.in(ex02_1_z));
  Ex02 ex02_1 (.Sb(Ex02), .Clock(button_2_out), .Reset(button_4_out), .Z(ex02_1_z));
  Ex03 ex03_1 (.Sb(Ex03), .Clock(button_5_out), .Reset(button_6_out), .Z(ex03_1_z));
  LED led_3 (.in(ex03_1_z));
endmodule

module Ex01 (
  input  Sb,
  input  Clock,
  input  Reset,
  output Z
);

  wire and_1_out, and_2_out, not_1_out, or_1_out, Q0_q, Q0_qn, Q1_q;

  D_Flip_Flop Q0 (.D(Sb), .clk(Clock), .Q(Q0_q), .Qn(Q0_qn), .reset(Reset));  // open: preset
  D_Flip_Flop Q1 (.D(or_1_out), .clk(Clock), .Q(Q1_q), .reset(Reset));  // open: Qn, preset
  and and_1 (and_1_out, Q1_q, Sb, Q0_qn);
  and and_2 (and_2_out, Q0_q, not_1_out);
  not not_1 (not_1_out, Sb);
  and and_3 (Z, Q0_q, Q1_q);
  or or_1 (or_1_out, and_1_out, and_2_out);
endmodule

module Ex02 (
  input  Sb,
  input  Clock,
  input  Reset,
  output Z
);

  wire and_2_out, not_1_out, Q0_q, Q1_q;

  and and_1 (Z, Sb, Q1_q);
  D_Flip_Flop Q0 (.D(Sb), .clk(Clock), .Q(Q0_q), .reset(Reset));  // open: Qn, preset
  and and_2 (and_2_out, Q0_q, not_1_out);
  D_Flip_Flop Q1 (.D(and_2_out), .clk(Clock), .Q(Q1_q), .reset(Reset));  // open: Qn, preset
  not not_1 (not_1_out, Sb);
endmodule

module Encoder (
  input  [3:0] in_1,
  output [1:0] I1I0
);

  wire and_1_out, and_2_out, and_3_out, and_4_out, and_5_out, and_6_out, and_7_out, not_1_out, not_2_out,
       not_3_out, not_4_out;

  not not_1 (not_1_out, in_1[3]);
  not not_2 (not_2_out, in_1[2]);
  not not_3 (not_3_out, in_1[1]);
  not not_4 (not_4_out, in_1[0]);
  and and_1 (and_1_out, not_2_out, not_3_out);
  and and_2 (and_2_out, not_2_out, not_4_out);
  and and_3 (and_3_out, not_1_out, not_3_out, in_1[0]);
  and and_4 (and_4_out, in_1[1], not_4_out);
  and and_5 (and_5_out, not_1_out, in_1[2], in_1[0]);
  and and_6 (and_6_out, in_1[3], not_2_out);
  and and_7 (and_7_out, in_1[2], in_1[1]);
  or or_1 (I1I0[0], not_4_out, in_1[2], in_1[3]);
  or or_2 (I1I0[1], and_1_out, and_2_out, and_3_out, and_4_out, and_5_out, and_6_out, and_7_out);
endmodule

module Ex03 (
  input  [3:0] Sb,
  input  Clock,
  input  Reset,
  output Z
);

  wire logic_ex03_1_d0, logic_ex03_1_d1, Q0_q, Q1_q;
  wire [1:0] encoder_1_i1i0;

  Encoder encoder_1 (.in_1(Sb), .I1I0(encoder_1_i1i0));
  D_Flip_Flop Q1 (.D(logic_ex03_1_d1), .clk(Clock), .Q(Q1_q), .reset(Reset));  // open: Qn, preset
  D_Flip_Flop Q0 (.D(logic_ex03_1_d0), .clk(Clock), .Q(Q0_q), .reset(Reset));  // open: Qn, preset
  Logic_Ex03 logic_ex03_1 (
    .Q1(Q1_q), .I1I0(encoder_1_i1i0), .Q0(Q0_q), .D1(logic_ex03_1_d1), .D0(logic_ex03_1_d0), .Z(Z));
endmodule

module Logic_Ex03 (
  input  Q1,
  input  [1:0] I1I0,
  input  Q0,
  output D1,
  output D0,
  output Z
);

  wire and_1_out, and_2_out, and_3_out, and_4_out, not_1_out, not_2_out, not_3_out, not_4_out;

  not not_1 (not_1_out, I1I0[1]);
  not not_2 (not_2_out, I1I0[0]);
  not not_3 (not_3_out, Q1);
  not not_4 (not_4_out, Q0);
  and and_1 (and_1_out, not_1_out, I1I0[0], not_3_out, Q0);
  and and_2 (and_2_out, I1I0[1], not_2_out, Q1, not_4_out);
  and and_3 (and_3_out, not_1_out, not_2_out);
  and and_4 (and_4_out, not_2_out, Q1, not_4_out);
  and and_5 (Z, Q1, Q0);
  or or_1 (D1, and_1_out, and_2_out);
  or or_2 (D0, and_3_out, and_4_out);
endmodule
