// Logisim project lab6.circ as structural Verilog: 10 circuits, main circuit main
module main (
  input  in_1,
  input  [1:0] in_2,
  input  [1:0] in_3,
  input  [7:0] in_4,
  input  [1:0] in_5,
  input  [7:0] in_6,
  input  in_7,
  input  in_8,
  input  [7:0] in_9,
  input  [14:0] in_10,
  input  in_11,
  input  in_12,
  input  in_13,
  input  [7:0] in_14,
  input  [12:0] in_15,
  input  [7:0] in_16,
  input  in_17,
  input  in_18,
  input  [14:0] in_19,
  input  in_20,
  input  in_21,
  input  [7:0] in_22,
  output [7:0] out_23,
  output [7:0] out_24,
  output [7:0] out_25,
  output [7:0] out_26,
  output [7:0] out_27,
  output [7:0] out_28
);

  wire clock_1_out, clock_2_out, clock_3_out, clock_4_out, clock_5_out;

  Clock clock_1 (.out(clock_1_out));
  Clock clock_2 (.out(clock_2_out));
  Clock clock_3 (.out(clock_3_out));
  Clock clock_4 (.out(clock_4_out));
  RAM ram_1 (.addr(in_6), .we(in_7), .oe(in_8), .clk(clock_5_out), .din(in_9), .dout(out_25));
  Clock clock_5 (.out(clock_5_out));
  Ex01 ex01_1 (
    .write(in_1), .write_reg(in_2), .read_reg_1(in_3), .write_data(in_4), .read_reg_2(in_5),
    .clock(clock_4_out), .read_data1(out_23), .read_data2(out_24));
  Ex02 ex02_1 (
    .address(in_10), .chip_select(in_11), .output_enable(in_12), .write_enable(in_13), .data_in(in_14),
    .clock(clock_1_out), .U(out_26));
  Ex03 ex03_1 (
    .address(in_15), .data_in(in_16), .write_enable(in_17), .output_enable(in_18), .clock(clock_2_out),
    .U(out_27));
  Ex04 ex04_1 (
    .address(in_19), .write_enable(in_20), .output_enable(in_21), .data_in(in_22), .clock(clock_3_out),
    .U(out_28));

  // Notes on the sheet:
  //   Ex01
  //   Ex02
  //   Store: if 1, store input in memory
  //   Load: if 1, load memory to output
  //   Input: value to be stored at address
  //   Address: location accessed memory
  //   Clock
  //   Data: valued loaded from address
endmodule

module \logic  (
  input  [7:0] Prev,
  input  [7:0] Data,
  input  Enable,
  output [7:0] out_4
);

  Multiplexer #(.width(8)) multiplexer_1 (.in0(Prev), .in1(Data), .out(out_4), .sel(Enable));
endmodule

module Ex01 (
  input  write,
  input  [1:0] write_reg,
  input  [1:0] read_reg_1,
  input  [7:0] write_data,
  input  [1:0] read_reg_2,
  input  clock,
  output [7:0] read_data1,
  output [7:0] read_data2
);

  wire decoder_1_out0, decoder_1_out1, decoder_1_out2, decoder_1_out3;
  wire [7:0] logic_1_out_4, logic_2_out_4, logic_3_out_4, logic_4_out_4, regis_1_u, regis_2_u, regis_3_u,
       regis_4_u;

  Decoder #(.select(2)) decoder_1 (
    .out0(decoder_1_out0), .out1(decoder_1_out1), .out2(decoder_1_out2), .out3(decoder_1_out3),
    .sel(write_reg), .en(write));
  \logic  logic_1 (.Prev(regis_1_u), .Data(write_data), .Enable(decoder_1_out0), .out_4(logic_1_out_4));
  \logic  logic_2 (.Prev(regis_2_u), .Data(write_data), .Enable(decoder_1_out1), .out_4(logic_2_out_4));
  \logic  logic_3 (.Prev(regis_3_u), .Data(write_data), .Enable(decoder_1_out2), .out_4(logic_3_out_4));
  \logic  logic_4 (.Prev(regis_4_u), .Data(write_data), .Enable(decoder_1_out3), .out_4(logic_4_out_4));
  regis regis_1 (.in_1(logic_1_out_4), .Clock(clock), .U(regis_1_u));
  regis regis_2 (.in_1(logic_2_out_4), .Clock(clock), .U(regis_2_u));
  regis regis_3 (.in_1(logic_3_out_4), .Clock(clock), .U(regis_3_u));
  regis regis_4 (.in_1(logic_4_out_4), .Clock(clock), .U(regis_4_u));
  Multiplexer #(.select(2), .width(8)) multiplexer_1 (
    .in0(regis_1_u), .in1(regis_2_u), .in2(regis_3_u), .in3(regis_4_u), .out(read_data1), .sel(read_reg_1));
  Multiplexer #(.select(2), .width(8)) multiplexer_2 (
    .in0(regis_1_u), .in1(regis_2_u), .in2(regis_3_u), .in3(regis_4_u), .out(read_data2), .sel(read_reg_2));
endmodule

module regis (
  input  [7:0] in_1,
  input  Clock,
  output [7:0] U
);

  D_Flip_Flop d_ff_1 (.D(in_1[0]), .clk(Clock), .Q(U[0]));  // open: Qn, preset, reset
  D_Flip_Flop d_ff_2 (.D(in_1[4]), .clk(Clock), .Q(U[4]));  // open: Qn, preset, reset
  D_Flip_Flop d_ff_3 (.D(in_1[1]), .clk(Clock), .Q(U[1]));  // open: Qn, preset, reset
  D_Flip_Flop d_ff_4 (.D(in_1[5]), .clk(Clock), .Q(U[5]));  // open: Qn, preset, reset
  D_Flip_Flop d_ff_5 (.D(in_1[2]), .clk(Clock), .Q(U[2]));  // open: Qn, preset, reset
  D_Flip_Flop d_ff_6 (.D(in_1[6]), .clk(Clock), .Q(U[6]));  // open: Qn, preset, reset
  D_Flip_Flop d_ff_7 (.D(in_1[3]), .clk(Clock), .Q(U[3]));  // open: Qn, preset, reset
  D_Flip_Flop d_ff_8 (.D(in_1[7]), .clk(Clock), .Q(U[7]));  // open: Qn, preset, reset
endmodule

module Ex02 (
  input  [14:0] address,
  input  chip_select,
  input  output_enable,
  input  write_enable,
  input  [7:0] data_in,
  input  clock,
  output [7:0] U
);

  wire controlled_buffer_1_out;
  wire [7:0] ram_1_dout;

  assign controlled_buffer_1_out = chip_select ? clock : 1'bz;  // Controlled_Buffer controlled_buffer_1
  RAM #(.addrWidth(15)) ram_1 (
    .addr(address), .we(write_enable), .oe(output_enable), .clk(controlled_buffer_1_out), .din(data_in),
    .dout(ram_1_dout));
  assign U = chip_select ? ram_1_dout : 8'bz;  // Controlled_Buffer controlled_buffer_2
endmodule

module Ex03 (
  input  [12:0] address,
  input  [7:0] data_in,
  input  write_enable,
  input  output_enable,
  input  clock,
  output [7:0] U
);

  wire controlled_buffer_1_out, controlled_buffer_2_out, controlled_buffer_3_out, controlled_buffer_4_out,
       controlled_buffer_5_out, decoder_1_out0, decoder_1_out1, decoder_1_out2, decoder_1_out3,
       decoder_1_out4, decoder_1_out5, decoder_1_out6, decoder_1_out7, or_1_out, or_2_out, or_3_out;
  wire [7:0] multiplexer_1_out, ram_1_dout, ram_2_dout, ram_3_dout, ram_4_dout, ram_5_dout;

  or or_1 (or_1_out, decoder_1_out2, decoder_1_out3);
  Decoder #(.select(3)) decoder_1 (
    .out0(decoder_1_out0), .out1(decoder_1_out1), .out2(decoder_1_out2), .out3(decoder_1_out3),
    .out4(decoder_1_out4), .out5(decoder_1_out5), .out6(decoder_1_out6), .out7(decoder_1_out7),
    .sel(address[12:10]), .en(1'b1));
  RAM #(.addrWidth(10)) ram_1 (
    .addr(address[9:0]), .we(write_enable), .oe(output_enable), .clk(controlled_buffer_1_out), .din(data_in),
    .dout(ram_1_dout));
  assign controlled_buffer_1_out = decoder_1_out0 ? clock : 1'bz;  // Controlled_Buffer controlled_buffer_1
  RAM #(.addrWidth(11)) ram_2 (
    .addr(address[10:0]), .we(write_enable), .oe(output_enable), .clk(controlled_buffer_2_out),
    .din(data_in), .dout(ram_2_dout));
  assign controlled_buffer_2_out = or_1_out ? clock : 1'bz;  // Controlled_Buffer controlled_buffer_2
  or or_2 (or_2_out, decoder_1_out5, decoder_1_out4);
  or or_3 (or_3_out, decoder_1_out7, decoder_1_out6);
  assign controlled_buffer_3_out = decoder_1_out1 ? clock : 1'bz;  // Controlled_Buffer controlled_buffer_3
  RAM #(.addrWidth(11)) ram_3 (
    .addr(address[10:0]), .we(write_enable), .oe(output_enable), .clk(controlled_buffer_4_out),
    .din(data_in), .dout(ram_3_dout));
  assign controlled_buffer_4_out = or_2_out ? clock : 1'bz;  // Controlled_Buffer controlled_buffer_4
  RAM #(.addrWidth(10)) ram_4 (
    .addr(address[9:0]), .we(write_enable), .oe(output_enable), .clk(controlled_buffer_3_out), .din(data_in),
    .dout(ram_4_dout));
  assign controlled_buffer_5_out = or_3_out ? clock : 1'bz;  // Controlled_Buffer controlled_buffer_5
  RAM #(.addrWidth(11)) ram_5 (
    .addr(address[10:0]), .we(write_enable), .oe(output_enable), .clk(controlled_buffer_5_out),
    .din(data_in), .dout(ram_5_dout));
  Multiplexer #(.select(3), .width(8)) multiplexer_1 (
    .in0(ram_1_dout), .in1(ram_4_dout), .in2(ram_2_dout), .in3(ram_2_dout), .in4(ram_3_dout),
    .in5(ram_3_dout), .in6(ram_5_dout), .in7(ram_5_dout), .out(multiplexer_1_out), .sel(address[12:10]));
  assign U = output_enable ? multiplexer_1_out : 8'bz;  // Controlled_Buffer controlled_buffer_6
endmodule

module Ex04 (
  input  [14:0] address,
  input  write_enable,
  input  output_enable,
  input  [7:0] data_in,
  input  clock,
  output [7:0] U
);

  wire d_ff_1_q, delay_logic_1_out_next, delay_logic_1_write_next, demultiplexer_1_out0,
       demultiplexer_1_out1, demultiplexer_1_out2, demultiplexer_1_out3, detect_address_change_1_out_3,
       detect_data_change_1_out_3, or_1_out;
  wire [7:0] controlled_buffer_2_out, controlled_buffer_3_out, controlled_buffer_4_out,
       controlled_buffer_5_out, ram_1_data;

  detect_address_change detect_address_change_1 (
    .address(address), .clock(clock), .out_3(detect_address_change_1_out_3));
  Demultiplexer #(.select(2)) demultiplexer_1 (
    .out0(demultiplexer_1_out0), .out1(demultiplexer_1_out1), .out2(demultiplexer_1_out2),
    .out3(demultiplexer_1_out3), .in(clock), .sel(address[14:13]));
  or or_1 (or_1_out, detect_address_change_1_out_3, detect_data_change_1_out_3);
  RAM #(.addrWidth(13), .databus("bidir")) ram_1 (
    .addr(address[12:0]), .we(delay_logic_1_write_next), .oe(delay_logic_1_out_next),
    .clk(demultiplexer_1_out0), .data(ram_1_data));
  RAM #(.addrWidth(13), .databus("bidir")) ram_2 (
    .addr(address[12:0]), .we(delay_logic_1_write_next), .oe(delay_logic_1_out_next),
    .clk(demultiplexer_1_out1), .data(ram_1_data));
  RAM #(.addrWidth(13), .databus("bidir")) ram_3 (
    .addr(address[12:0]), .we(delay_logic_1_write_next), .oe(delay_logic_1_out_next),
    .clk(demultiplexer_1_out2), .data(ram_1_data));
  RAM #(.addrWidth(13), .databus("bidir")) ram_4 (
    .addr(address[12:0]), .we(delay_logic_1_write_next), .oe(delay_logic_1_out_next),
    .clk(demultiplexer_1_out3), .data(ram_1_data));
  delay_logic delay_logic_1 (
    .write_enable(write_enable), .out_enable(output_enable), .change(or_1_out),
    .write_next(delay_logic_1_write_next), .out_next(delay_logic_1_out_next));
  assign ram_1_data = delay_logic_1_write_next ? data_in : 8'bz;  // Controlled_Buffer controlled_buffer_1
  D_Flip_Flop d_ff_1 (.D(delay_logic_1_out_next), .clk(clock), .Q(d_ff_1_q));  // open: Qn, preset, reset
  assign controlled_buffer_2_out = d_ff_1_q ? ram_1_data : 8'bz;  // Controlled_Buffer controlled_buffer_2
  assign controlled_buffer_3_out = d_ff_1_q ? ram_1_data : 8'bz;  // Controlled_Buffer controlled_buffer_3
  assign controlled_buffer_4_out = d_ff_1_q ? ram_1_data : 8'bz;  // Controlled_Buffer controlled_buffer_4
  assign controlled_buffer_5_out = d_ff_1_q ? ram_1_data : 8'bz;  // Controlled_Buffer controlled_buffer_5
  Multiplexer #(.select(2), .width(8)) multiplexer_1 (
    .in0(controlled_buffer_2_out), .in1(controlled_buffer_3_out), .in2(controlled_buffer_4_out),
    .in3(controlled_buffer_5_out), .out(U), .sel(address[14:13]));
  detect_data_change detect_data_change_1 (.data(data_in), .clock(clock), .out_3(detect_data_change_1_out_3));
endmodule

module delay_logic (
  input  write_enable,
  input  out_enable,
  input  change,
  output write_next,
  output out_next
);

  wire and_1_out, and_2_out, and_3_out, and_4_out, not_1_out, not_2_out, not_3_out;

  not not_1 (not_1_out, write_enable);
  not not_2 (not_2_out, out_enable);
  not not_3 (not_3_out, change);
  and and_1 (and_1_out, write_enable, not_2_out);
  and and_2 (and_2_out, write_enable, change);
  and and_3 (and_3_out, not_1_out, out_enable);
  and and_4 (and_4_out, out_enable, not_3_out);
  or or_1 (write_next, and_1_out, and_2_out);
  or or_2 (out_next, and_3_out, and_4_out);
endmodule

module detect_address_change (
  input  [14:0] address,
  input  clock,
  output out_3
);

  wire [14:0] d_ff_1_q, xor_1_out;

  D_Flip_Flop d_ff_1 (.D(address[0]), .clk(clock), .Q(d_ff_1_q[0]));  // open: Qn, preset, reset
  D_Flip_Flop d_ff_2 (.D(address[1]), .clk(clock), .Q(d_ff_1_q[1]));  // open: Qn, preset, reset
  D_Flip_Flop d_ff_3 (.D(address[2]), .clk(clock), .Q(d_ff_1_q[2]));  // open: Qn, preset, reset
  D_Flip_Flop d_ff_4 (.D(address[3]), .clk(clock), .Q(d_ff_1_q[3]));  // open: Qn, preset, reset
  D_Flip_Flop d_ff_5 (.D(address[4]), .clk(clock), .Q(d_ff_1_q[4]));  // open: Qn, preset, reset
  D_Flip_Flop d_ff_6 (.D(address[5]), .clk(clock), .Q(d_ff_1_q[5]));  // open: Qn, preset, reset
  D_Flip_Flop d_ff_7 (.D(address[6]), .clk(clock), .Q(d_ff_1_q[6]));  // open: Qn, preset, reset
  D_Flip_Flop d_ff_8 (.D(address[7]), .clk(clock), .Q(d_ff_1_q[7]));  // open: Qn, preset, reset
  D_Flip_Flop d_ff_9 (.D(address[8]), .clk(clock), .Q(d_ff_1_q[8]));  // open: Qn, preset, reset
  D_Flip_Flop d_ff_10 (.D(address[9]), .clk(clock), .Q(d_ff_1_q[9]));  // open: Qn, preset, reset
  D_Flip_Flop d_ff_11 (.D(address[10]), .clk(clock), .Q(d_ff_1_q[10]));  // open: Qn, preset, reset
  D_Flip_Flop d_ff_12 (.D(address[11]), .clk(clock), .Q(d_ff_1_q[11]));  // open: Qn, preset, reset
  D_Flip_Flop d_ff_13 (.D(address[12]), .clk(clock), .Q(d_ff_1_q[12]));  // open: Qn, preset, reset
  D_Flip_Flop d_ff_14 (.D(address[13]), .clk(clock), .Q(d_ff_1_q[13]));  // open: Qn, preset, reset
  D_Flip_Flop d_ff_15 (.D(address[14]), .clk(clock), .Q(d_ff_1_q[14]));  // open: Qn, preset, reset
  assign xor_1_out = address ^ d_ff_1_q;  // XOR_Gate xor_1, 15 bits wide
  or or_1 (out_3, xor_1_out[14], xor_1_out[13], xor_1_out[12], xor_1_out[11], xor_1_out[10], xor_1_out[9], xor_1_out[8], xor_1_out[7], xor_1_out[6], xor_1_out[5], xor_1_out[4], xor_1_out[3], xor_1_out[2], xor_1_out[1], xor_1_out[0]);
endmodule

module detect_data_change (
  input  [7:0] data,
  input  clock,
  output out_3
);

  wire d_ff_9_q, d_ff_10_q, d_ff_11_q, d_ff_12_q, d_ff_13_q, undriven, undriven_2, undriven_3, undriven_4,
       undriven_5;
  wire [7:0] d_ff_1_q, xor_1_out;

  D_Flip_Flop d_ff_1 (.D(data[0]), .clk(clock), .Q(d_ff_1_q[0]));  // open: Qn, preset, reset
  D_Flip_Flop d_ff_2 (.D(data[1]), .clk(clock), .Q(d_ff_1_q[1]));  // open: Qn, preset, reset
  D_Flip_Flop d_ff_3 (.D(data[2]), .clk(clock), .Q(d_ff_1_q[2]));  // open: Qn, preset, reset
  D_Flip_Flop d_ff_4 (.D(data[3]), .clk(clock), .Q(d_ff_1_q[3]));  // open: Qn, preset, reset
  D_Flip_Flop d_ff_5 (.D(data[4]), .clk(clock), .Q(d_ff_1_q[4]));  // open: Qn, preset, reset
  D_Flip_Flop d_ff_6 (.D(data[5]), .clk(clock), .Q(d_ff_1_q[5]));  // open: Qn, preset, reset
  D_Flip_Flop d_ff_7 (.D(data[6]), .clk(clock), .Q(d_ff_1_q[6]));  // open: Qn, preset, reset
  D_Flip_Flop d_ff_8 (.D(data[7]), .clk(clock), .Q(d_ff_1_q[7]));  // open: Qn, preset, reset
  D_Flip_Flop d_ff_9 (.D(undriven_5), .clk(clock), .Q(d_ff_9_q));  // open: Qn, preset, reset
  D_Flip_Flop d_ff_10 (.D(undriven_4), .clk(clock), .Q(d_ff_10_q));  // open: Qn, preset, reset
  D_Flip_Flop d_ff_11 (.D(undriven_3), .clk(clock), .Q(d_ff_11_q));  // open: Qn, preset, reset
  D_Flip_Flop d_ff_12 (.D(undriven_2), .clk(clock), .Q(d_ff_12_q));  // open: Qn, preset, reset
  D_Flip_Flop d_ff_13 (.D(undriven), .clk(clock), .Q(d_ff_13_q));  // open: Qn, preset, reset
  assign xor_1_out = data ^ d_ff_1_q;  // XOR_Gate xor_1, 8 bits wide
  or or_1 (out_3, xor_1_out[7], xor_1_out[6], xor_1_out[5], xor_1_out[4], xor_1_out[3], xor_1_out[2], xor_1_out[1], xor_1_out[0]);
endmodule
